# Fritzing sketch 2x16_Devre_Semasi (saved by Fritzing 0.9.2b)
breadboards: 1

parts:
  Raspberry_Pi1 = Raspberry Pi 2
  LCD1 = LCD screen
  U1 = POT [package=pot_alpha_rv16af-20]

nets:
  3V3: Raspberry_Pi1.3v3, Raspberry_Pi1.3V3, Raspberry_Pi1.GPIO24, Raspberry_Pi1.5V, LCD1.VSS, LCD1.VDD, LCD1.R/W, LCD1.LED+, LCD1.LED-, U1.A, U1.E
  N1: Raspberry_Pi1.GPIO17, LCD1.E
  N2: Raspberry_Pi1.GPIO22, LCD1.RS
  N3: Raspberry_Pi1.GPIO9, Raspberry_Pi1.GPIO25, LCD1.DB4
  N4: Raspberry_Pi1.GPIO23, LCD1.DB7
  N5: Raspberry_Pi1.GPIO18, LCD1.DB5
  N6: LCD1.V0, U1.S
